# Fritzing sketch Esquema cleverclock (saved by Fritzing 0.9.3b)
breadboards: 1

parts:
  Componente1 = Arduino Uno (Rev3)
  Nokia_5110_LCD_Module1 = Nokia 5110 LCD
  Part2 = Bluetooth HC-05 Macho

nets:
  N1: Componente1.D10_PWM/SS, Part2.TXD
  N2: Componente1.D11_PWM/MOSI, Part2.RXD
  N3: Componente1.D3_PWM, Nokia_5110_LCD_Module1.VCC, Nokia_5110_LCD_Module1.VCC_(out)
  N4: Componente1.D4, Nokia_5110_LCD_Module1.GND, Nokia_5110_LCD_Module1.GND_(out)
  N5: Componente1.D5_PWM, Nokia_5110_LCD_Module1.SCE, Nokia_5110_LCD_Module1.SCE_(out)
  N6: Componente1.D6_PWM, Nokia_5110_LCD_Module1.RST, Nokia_5110_LCD_Module1.RST_(out)
  N7: Componente1.D7, Nokia_5110_LCD_Module1.D/C, Nokia_5110_LCD_Module1.D/C_(out)
  5V: Componente1.5V, Nokia_5110_LCD_Module1.DN(MOSI), Nokia_5110_LCD_Module1.DN(MODI)_(out), Part2.VCC
  GND: Componente1.GND, Nokia_5110_LCD_Module1.SCLK, Nokia_5110_LCD_Module1.LED, Nokia_5110_LCD_Module1.SCLK_(out), Nokia_5110_LCD_Module1.LED_(out), Part2.GND

custom parts:
  Nokia 5110 LCD: Nokia 5110 Graphic 84*48 LCD module such as the Sparkfun LCD-10168 or the clones from Ebay. There is example code for the Arduino available from the Sparkfun site in https://learn.sparkfun.com/tutorials/graphic-lcd-hookup-guide This is a 3.3V device, if you are running it from a 5V micro you need a 5V tolorant level translator such as the 74ahc367 to protect the signal imputs. Rafa G. did a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
